// Logisim project SIMULATION_NO_2.circ as structural Verilog
module PROBLEM_2 (
  input  X,
  input  Y,
  input  Z,
  output F
);

  wire and_1_out, and_2_out, and_3_out;

  and and_1 (and_1_out, Y, Z);
  and and_2 (and_2_out, X, Z);
  and and_3 (and_3_out, X, Y);
  or or_1 (F, and_1_out, and_2_out, and_3_out);
endmodule
