// Logisim project SIMULATION_NO_8.circ as structural Verilog
module P8 (
  input  A,
  input  B,
  input  C,
  input  D,
  output R
);

  wire and_1_out, and_2_out, and_3_out, and_4_out;

  and and_1 (and_1_out, B, C, D);
  and and_2 (and_2_out, A, C, D);
  and and_3 (and_3_out, A, B, D);
  and and_4 (and_4_out, A, B, C);
  or or_1 (R, and_1_out, and_2_out, and_3_out, and_4_out);
endmodule
